// Logisim project task_10.circ as structural Verilog: 1 circuit, main circuit main
module main (
  input  in_1,
  input  in_2,
  input  in_3,
  input  in_4,
  output out_5,
  output out_6,
  output out_7,
  output out_8
);

  wire and_1_out, and_4_out, and_5_out, not_1_out, not_2_out, or_1_out;

  and and_1 (and_1_out, in_3, in_1);
  and and_2 (out_8, in_2, in_4);
  and and_3 (out_5, and_1_out, out_8);
  and and_4 (and_4_out, in_2, in_3);
  and and_5 (and_5_out, in_1, in_4);
  not not_1 (not_1_out, out_8);
  not not_2 (not_2_out, out_5);
  or or_1 (or_1_out, and_4_out, and_5_out);
  and and_6 (out_6, not_1_out, and_1_out);
  and and_7 (out_7, not_2_out, or_1_out);
endmodule
