// Logisim project task_6.circ as structural Verilog: 1 circuit, main circuit main
module main (
  input  in_1,
  input  in_2,
  input  in_3,
  output out_4,
  output out_5
);

  wire and_1_out, and_2_out, nand_1_out, nor_1_out, nor_2_out, or_1_out;

  and and_1 (and_1_out, in_1, in_2);
  and and_2 (and_2_out, and_1_out, in_3);
  nor nor_1 (nor_1_out, and_1_out, in_3);
  nor nor_2 (nor_2_out, and_2_out, nor_1_out);
  and and_3 (out_4, in_1, nor_2_out);
  or or_1 (or_1_out, in_1, in_2);
  nand nand_1 (nand_1_out, in_2, nor_2_out);
  nand nand_2 (out_5, or_1_out, nand_1_out);
endmodule
