// Logisim project task_7.circ as structural Verilog: 1 circuit, main circuit main
module main (
  input  in_1,
  input  in_2,
  input  in_3,
  input  in_4,
  input  in_5,
  input  in_6,
  output out_7,
  output out_8,
  output out_9,
  output out_10
);

  wire nand_1_out, nand_2_out, nand_3_out, nand_4_out, nand_5_out, nand_6_out, nand_7_out, nand_8_out,
       nor_1_out, nor_2_out, nor_3_out, nor_4_out, nor_5_out, nor_6_out, nor_7_out, nor_8_out, nor_9_out,
       nor_10_out, nor_11_out;

  // XOR_Gate xor_1 is placed but not wired
  nand nand_1 (nand_1_out, in_1, in_1);
  nand nand_2 (nand_2_out, in_2, in_2);
  nand nand_3 (nand_3_out, in_2, in_2);
  nand nand_4 (nand_4_out, in_3, in_3);
  nand nand_5 (nand_5_out, in_3, in_3);
  nand nand_6 (nand_6_out, in_4, in_4);
  nor nor_1 (nor_1_out, nand_1_out, in_2);
  nor nor_2 (nor_2_out, in_1, nand_2_out);
  nor nor_3 (nor_3_out, nand_3_out, in_3);
  nor nor_4 (nor_4_out, in_2, nand_4_out);
  nor nor_5 (nor_5_out, nand_5_out, in_4);
  nor nor_6 (nor_6_out, in_3, nand_6_out);
  nand nand_7 (nand_7_out, in_5, in_6);
  nor nor_7 (nor_7_out, in_6, in_5);
  nand nand_8 (nand_8_out, nand_7_out, nand_7_out);
  nor nor_8 (nor_8_out, nor_1_out, nor_2_out);
  nor nor_9 (nor_9_out, nor_3_out, nor_4_out);
  nor nor_10 (nor_10_out, nor_5_out, nor_6_out);
  // NOT_Gate not_1 is placed but not wired
  nor nor_11 (nor_11_out, nand_8_out, nor_7_out);
  nand nand_9 (out_8, nor_8_out, nor_8_out);
  nand nand_10 (out_9, nor_9_out, nor_9_out);
  nand nand_11 (out_10, nor_10_out, nor_10_out);

  assign out_7 = in_1;
endmodule
