// Logisim project task_8.circ as structural Verilog: 3 circuits, main circuit half_subtractor
module main (
  input  in_1,
  input  in_2,
  input  in_3,
  input  in_4,
  input  in_5,
  input  in_6,
  input  in_7,
  input  in_8,
  output out_9,
  output out_10,
  output out_11,
  output out_12
);

  wire and_1_out, m_subtractor_1_out_4, m_subtractor_1_out_5, m_subtractor_2_out_4, m_subtractor_2_out_5,
       m_subtractor_3_out_4, m_subtractor_3_out_5, m_subtractor_4_out_4, m_subtractor_4_out_5, not_1_out,
       not_2_out;

  not not_1 (not_1_out, in_8);
  and and_1 (and_1_out, not_1_out, in_8);
  m_subtractor m_subtractor_1 (
    .in_1(m_subtractor_2_out_5), .in_2(in_5), .in_3(in_1), .out_4(m_subtractor_1_out_4),
    .out_5(m_subtractor_1_out_5));
  m_subtractor m_subtractor_2 (
    .in_1(m_subtractor_3_out_5), .in_2(in_6), .in_3(in_2), .out_4(m_subtractor_2_out_4),
    .out_5(m_subtractor_2_out_5));
  m_subtractor m_subtractor_3 (
    .in_1(m_subtractor_4_out_5), .in_2(in_7), .in_3(in_3), .out_4(m_subtractor_3_out_4),
    .out_5(m_subtractor_3_out_5));
  m_subtractor m_subtractor_4 (
    .in_1(and_1_out), .in_2(in_8), .in_3(in_4), .out_4(m_subtractor_4_out_4), .out_5(m_subtractor_4_out_5));
  not not_2 (not_2_out, m_subtractor_1_out_5);
  and and_2 (out_9, m_subtractor_1_out_4, not_2_out);
  and and_3 (out_10, m_subtractor_2_out_4, not_2_out);
  and and_4 (out_11, m_subtractor_3_out_4, not_2_out);
  and and_5 (out_12, m_subtractor_4_out_4, not_2_out);
endmodule

module half_subtractor (
  input  in_1,
  input  in_2,
  output out_3,
  output out_4
);

  wire and_1_out, not_1_out, not_2_out;

  not not_1 (not_1_out, in_2);
  and and_1 (and_1_out, in_1, not_1_out);
  not not_2 (not_2_out, in_1);
  and and_2 (out_4, not_2_out, in_2);
  or or_1 (out_3, and_1_out, out_4);
endmodule

module m_subtractor (
  input  in_1,
  input  in_2,
  input  in_3,
  output out_4,
  output out_5
);

  wire half_subtractor_1_out_3, half_subtractor_1_out_4, half_subtractor_2_out_4, nand_1_out, nand_2_out;

  half_subtractor half_subtractor_1 (
    .in_1(in_2), .in_2(in_1), .out_3(half_subtractor_1_out_3), .out_4(half_subtractor_1_out_4));
  nand nand_1 (nand_1_out, half_subtractor_1_out_4, half_subtractor_1_out_4);
  nand nand_2 (nand_2_out, half_subtractor_2_out_4, half_subtractor_2_out_4);
  half_subtractor half_subtractor_2 (
    .in_1(half_subtractor_1_out_3), .in_2(in_3), .out_3(out_4), .out_4(half_subtractor_2_out_4));
  nand nand_3 (out_5, nand_1_out, nand_2_out);
endmodule
